# Fritzing sketch Smart-Water-Management-circuit (saved by Fritzing 0.9.3b)

parts:
  Part1 = Arduino Uno (Rev3)
  S1 = PH meter [package=THT]
  U1 = ESP8266 NodeMCU LoLin module
  Part2 = Soil Moisture Sensor
  DS1 = DS18B20 1-Wire Temperature Sensor [part_number=DS18B20]
  R2 = Resistor [tolerance=±5% resistance=10k package=THT]  # not connected
  BAT1 = BC9VPC [package=bc9vpc]

nets:
  N1: Part1.A0, S1.pin1
  N2: Part1.A5/SCL, Part2.SIG
  N3: Part1.D0/RX, U1.TX
  N4: Part1.D1/TX, U1.RX
  N5: Part1.D2, DS1.DQ
  N6: Part1.5V, S1.pin2
  GND: Part1.GND, S1.pin3, DS1.GND
  N7: Part1.VIN, BAT1.V+
  GND_2: U1.GND, Part2.GND
  VIN: U1.Vin, Part2.VCC

custom parts:
  ESP8266 NodeMCU LoLin module: ESP8266 based NodeMCU

// code stored in the sketch: Untitled2.ino
//include libraries
#include <SoftwareSerial.h>
#include <LiquidCrystal.h>

//for  bluetooth - create an object called BTserial, with RX pin at 3 and TX pin at 2
SoftwareSerial  BTserial(3,2); // RX | TX

//decraration of all our variables

float  reads;
int pin = A0;

float vOut = 0 ;//voltage drop across 2 points
float  vIn = 5;
float R1 = 1000;
float R2 = 0;
float buffer = 0;
float TDS;

float  R = 0;//resistance between the 2 wires
float r = 0;//resistivity 
float L  = 0.06;//distance between the wires in m
double A = 0.000154;//area of cross  section of wire in m^2

float C = 0;//conductivity in S/m
float Cm = 0;//conductivity  in mS/cm

int rPin = 9;
int bPin = 5;
int gPin = 6;
int rVal = 255;
int  bVal = 255;
int gVal = 255;

//we will use this formula to get the resistivity  after using ohm's law -> R = r L/A => r = R A/L

//creating lcd object from  Liquid Crystal library
LiquidCrystal lcd(7,8,10,11,12,13);

void setup()  {
  //initialise BT serial and   serial monitor
  Serial.begin(9600);
  BTserial.begin(9600);

  //initialise lcd
  lcd.begin(16, 2);

  //set rgb led pins (all to be pwm pins on Arduino) as output
  pinMode(rPin,OUTPUT);
  pinMode(bPin,OUTPUT);
  pinMode(gPin,OUTPUT);
  pinMode(pin,INPUT);
  //Print stagnant message to LCD
  lcd.print("Conductivity: ");
}

void  loop() {
    reads = analogRead(A0);
  
  vOut = reads*5/1023;
  Serial.println(reads);
//  Serial.println(vOut);
  buffer = (vIn/vOut)-1;
  R2 = R1*buffer;
  Serial.println(R2);
  delay(500);
    //convert voltage to resistance
    //Apply formula mentioned  above
      r = R2*A/L;//R=rL/A
    //convert resistivity to condictivity
    C = 1/r;
    Cm = C*10;
    //convert conductivity in mS/cm to TDS
    TDS = Cm *700;
    //Set cursor of LCD to next row
    lcd.setCursor(0,1);
    lcd.println(C);

    //display corresponding colours on rgb led according  to the analog read
     if( reads < 600 )
  {
      if (reads <= 300){
        setColor( 255, 0, 255 ) ;
      }
      if (reads > 200){
        setColor(  200, 0, 255 ) ;
      }
  }
  else{
    if( reads <= 900 )
    {
      setColor( 0, 0, 255 ) ;
    }
    if( reads > 700 )
  {
    setColor(  0, 255, 255 ) ;
  }
    }

//send data to Ardutooth app on mobile phone  through bluetooth
BTserial.print(C);
BTserial.print(",");
BTserial.print(TDS);
BTserial.print(";");
delay(500);
}


void  setColor(int red, int green, int blue)
{
  analogWrite( rPin, 255 - red )  ;
  analogWrite( gPin, 255 - green ) ;
  analogWrite( bPin, 255 - blue ) ;  
}
